# Fritzing sketch Circuit_scheme (saved by Fritzing 1.0.1rc)
breadboards: 1

parts:
  Button_2 = Pushbutton [package="[THT]"]
  R16 = Resistor [tolerance=±5% power=0.25 resistance=220 package=THT]
  Q1_-_C2274F = NPN-Transistor [package="TO92 [THT]"]
  D2 = Rectifier Diode [part_number=1N4001 package="300 mil [THT]"]
  Q1_-_C2274F1 = NPN-Transistor [package="TO92 [THT]"]
  Switch_B = Pushbutton [package="[THT]"]
  R10 = Resistor [tolerance=±5% power=0.25 resistance=220 package=THT]  # not connected
  Switch_C = Pushbutton [package="[THT]"]
  Q1_-_C2274F2 = NPN-Transistor [package="TO92 [THT]"]
  R9 = Resistor [tolerance=±5% power=0.25 resistance=4.7k package=THT]
  R15 = Resistor [tolerance=±5% power=0.25 resistance=220 package=THT]
  Arduino_UNO = Arduino Uno (Rev3)
  R14 = Resistor [tolerance=±5% power=0.25 resistance=220 package=THT]
  Relé_2_-_48V1 = RELAY [package=OJ]
  R12 = Resistor [tolerance=±5% power=0.25 resistance=220 package=THT]
  Button_1 = Pushbutton [package="[THT]"]
  R11 = Resistor [tolerance=±5% power=0.25 resistance=220 package=THT]  # not connected
  Relé_1_-_48V = RELAY [package=OJ]
  R7 = Resistor [tolerance=±5% power=0.25 resistance=4.7k package=THT]
  D1 = Rectifier Diode [part_number=1N4001 package="300 mil [THT]"]
  R8 = Resistor [tolerance=±5% power=0.25 resistance=4.7k package=THT]
  D3 = Rectifier Diode [part_number=1N4001 package="300 mil [THT]"]
  Relé_3_-_48V2 = RELAY [package=OJ]
  Button_3 = Pushbutton [package="[THT]"]
  Switch_A = Pushbutton [package="[THT]"]

nets:
  N1: Button_2.Pin_1, Button_2.Pin_3, Button_2.Pin_4, Switch_B.Pin_1, Switch_B.Pin_2, Switch_C.Pin_1, Switch_C.Pin_2, Arduino_UNO.5V, Button_1.Pin_3, Button_1.Pin_4, Button_3.Pin_1, Button_3.Pin_2, Switch_A.Pin_1
  N2: R16.Pin_0, R16.Pin_1, Switch_C.Pin_3, Switch_C.Pin_4, Arduino_UNO.D8, R12.Pin_0
  N3: Q1_-_C2274F.B, R7.Pin_0
  48V: Q1_-_C2274F.C, D2.cathode, Q1_-_C2274F1.C, Relé_2_-_48V1.COIL2, Relé_2_-_48V1.COIL1, Relé_1_-_48V.COIL2, Relé_1_-_48V.COIL1, D1.cathode, Relé_3_-_48V2.COIL1
  N4: Q1_-_C2274F1.B, R8.Pin_0
  N5: Switch_B.Pin_3, Switch_B.Pin_4, R15.Pin_0, Arduino_UNO.D7
  N6: Q1_-_C2274F2.B, R9.Pin_0
  N7: Q1_-_C2274F2.C, D3.anode, Relé_3_-_48V2.COIL2
  N8: R9.Pin_1, Arduino_UNO.D12/MISO
  N9: Arduino_UNO.D10_PWM/SS, R7.Pin_1
  N10: Arduino_UNO.D11_PWM/MOSI, R8.Pin_1
  GND: Arduino_UNO.D3_PWM, Arduino_UNO.D4, Arduino_UNO.D5_PWM
  N11: Arduino_UNO.D6_PWM, R14.Pin_0, Switch_A.Pin_3, Switch_A.Pin_4
  N12: Button_1.Pin_1, Button_1.Pin_2

notes:
  Multi Switch 4
  Multi Switch 2
  Multi Switch 3
  Relé actuation
  Switch Section
