# Fritzing sketch Circuit_scheme (saved by Fritzing 1.0.1rc)
breadboards: 1

parts:
  Arduino_UNO = Arduino Uno (Rev3)
  Relé_1_-_48V = RELAY [package=OJ]
  D1 = Rectifier Diode [part_number=1N4001 package="300 mil [THT]"]
  Q1_-_C2274F = NPN-Transistor [package="TO92 [THT]"]
  R7 = Resistor [tolerance=±5% power=0.25 resistance=4.7k package=THT]
  Relé_2_-_48V1 = RELAY [package=OJ]
  D2 = Rectifier Diode [part_number=1N4001 package="300 mil [THT]"]
  Q1_-_C2274F1 = NPN-Transistor [package="TO92 [THT]"]
  R8 = Resistor [tolerance=±5% power=0.25 resistance=4.7k package=THT]
  Relé_3_-_48V2 = RELAY [package=OJ]
  D3 = Rectifier Diode [part_number=1N4001 package="300 mil [THT]"]
  Q1_-_C2274F2 = NPN-Transistor [package="TO92 [THT]"]
  R9 = Resistor [tolerance=±5% power=0.25 resistance=4.7k package=THT]
  Switch_B = Pushbutton [package="[THT]"]
  Switch_A = Pushbutton [package="[THT]"]
  Switch_C = Pushbutton [package="[THT]"]
  R14 = Resistor [tolerance=±5% power=0.25 resistance=220 package=THT]
  R15 = Resistor [tolerance=±5% power=0.25 resistance=220 package=THT]
  R16 = Resistor [tolerance=±5% power=0.25 resistance=220 package=THT]
  Switch_read = Pushbutton [package="[THT]"]
  R17 = Resistor [tolerance=±5% power=0.25 resistance=220 package=THT]

nets:
  SDA: Arduino_UNO.A4/SDA
  N1: Arduino_UNO.D8, Switch_C.Pin_3, Switch_C.Pin_4, R16.Pin_0
  N2: Arduino_UNO.D9_PWM, Switch_read.Pin_3, Switch_read.Pin_4, R17.Pin_0
  N3: Arduino_UNO.D10_PWM/SS, R7.Pin_1
  N4: Arduino_UNO.D11_PWM/MOSI, R8.Pin_1
  N5: Arduino_UNO.D12/MISO, R9.Pin_1
  SCK: Arduino_UNO.A5/SCL
  N6: Arduino_UNO.D6_PWM, Switch_A.Pin_3, Switch_A.Pin_4, R14.Pin_0
  N7: Arduino_UNO.D7, Switch_B.Pin_3, Switch_B.Pin_4, R15.Pin_0
  Vcc: Arduino_UNO.5V, Switch_B.Pin_1, Switch_B.Pin_2, Switch_A.Pin_1, Switch_C.Pin_1, Switch_C.Pin_2, Switch_read.Pin_1, Switch_read.Pin_2
  48V: Relé_1_-_48V.COIL2, Relé_1_-_48V.COIL1, D1.cathode, Q1_-_C2274F.C, Relé_2_-_48V1.COIL2, Relé_2_-_48V1.COIL1, D2.cathode, Q1_-_C2274F1.C, Relé_3_-_48V2.COIL1
  N8: Q1_-_C2274F.B, R7.Pin_0
  N9: Q1_-_C2274F1.B, R8.Pin_0
  N10: Relé_3_-_48V2.COIL2, D3.anode, Q1_-_C2274F2.C
  N11: Q1_-_C2274F2.B, R9.Pin_0
  GND: R14.Pin_1, R16.Pin_1, R17.Pin_1

notes:
  Relé_1
  Multi Switch 4
  Multi Switch 2
  Multi Switch 3
  Relé actuation
  Switch Section
  LCD 2004 display
  (20 characters x 4 lines)
  MCP23017
  KEYPAD
  1 2 3
  4 5 6
  7 8 9
  * 0 #
  Arduino Uno:
  - SDA → A4
  - SCL → A5
  Arduino M0/Zero:
  - dedicated pin
  Arduino Mega 2560
  - SDA → Pin 20
  - SCL → Pin 21
